// Logisim project alu.circ as structural Verilog
module _8bit_AND (
  input  [7:0] A,
  input  [7:0] B,
  output [7:0] Output
);

  and and_1 (Output[0], A[0], B[0]);
  and and_2 (Output[1], A[1], B[1]);
  and and_3 (Output[2], A[2], B[2]);
  and and_4 (Output[3], A[3], B[3]);
  and and_5 (Output[4], A[4], B[4]);
  and and_6 (Output[5], A[5], B[5]);
  and and_7 (Output[6], A[6], B[6]);
  and and_8 (Output[7], A[7], B[7]);
endmodule

module _8bit_OR (
  input  [7:0] A,
  input  [7:0] B,
  output [7:0] Output
);

  or or_1 (Output[0], A[0], B[0]);
  or or_2 (Output[1], A[1], B[1]);
  or or_3 (Output[2], A[2], B[2]);
  or or_4 (Output[3], A[3], B[3]);
  or or_5 (Output[4], A[4], B[4]);
  or or_6 (Output[5], A[5], B[5]);
  or or_7 (Output[6], A[6], B[6]);
  or or_8 (Output[7], A[7], B[7]);
endmodule

module _8bit_XOR (
  input  [7:0] A,
  input  [7:0] B,
  output [7:0] Output
);

  xor xor_1 (Output[0], A[0], B[0]);
  xor xor_2 (Output[1], A[1], B[1]);
  xor xor_3 (Output[2], A[2], B[2]);
  xor xor_4 (Output[3], A[3], B[3]);
  xor xor_5 (Output[4], A[4], B[4]);
  xor xor_6 (Output[5], A[5], B[5]);
  xor xor_7 (Output[6], A[6], B[6]);
  xor xor_8 (Output[7], A[7], B[7]);
endmodule

module _8bit_add_sub (
  input  Control,
  input  [7:0] A,
  input  [7:0] B,
  output [7:0] Output
);

  wire adder_1_cout, adder_2_cout, adder_3_cout, adder_4_cout, adder_5_cout, adder_6_cout, adder_7_cout;

  Adder #(.width(1)) adder_1 (.cin(Control), .cout(adder_1_cout));  // open: a, b, out
  Adder #(.width(1)) adder_2 (.cin(adder_1_cout), .cout(adder_2_cout));  // open: a, b, out
  Adder #(.width(1)) adder_3 (.cin(adder_2_cout), .cout(adder_3_cout));  // open: a, b, out
  Adder #(.width(1)) adder_4 (.cin(adder_3_cout), .cout(adder_4_cout));  // open: a, b, out
  Adder #(.width(1)) adder_5 (.cin(adder_4_cout), .cout(adder_5_cout));  // open: a, b, out
  Adder #(.width(1)) adder_6 (.cin(adder_5_cout), .cout(adder_6_cout));  // open: a, b, out
  Adder #(.width(1)) adder_7 (.cin(adder_6_cout), .cout(adder_7_cout));  // open: a, b, out
  Adder #(.width(1)) adder_8 (.cin(adder_7_cout));  // open: a, b, out, cout
endmodule
